// Logisim project project0527.circ as structural Verilog: 7 circuits, main circuit main
module main (
);

  wire [31:0] ID_a, if_1_instruction;

  IF if_1 (.Instruction(if_1_instruction));  // open: in_1, in_2
  ID ID (.A(ID_a));  // open: C, Instruction, imm, Load, B
  ALU Ex (.A(ID_a));  // open: B, ALU_op, C
endmodule

module IF (
  input  [31:0] in_1,
  input  in_2,
  output [31:0] Instruction
);

  wire clock_1_out;
  wire [31:0] adder_1_out, register_1_q;

  Register #(.width(32)) register_1 (.D(adder_1_out), .Q(register_1_q), .clk(clock_1_out), .clr(in_2));  // open: en
  Clock clock_1 (.out(clock_1_out));
  Adder #(.width(32)) adder_1 (.a(in_1), .b(register_1_q), .out(adder_1_out));  // open: cin, cout
  ROM #(.dataWidth(32)) rom_1 (.addr(register_1_q[9:2]), .data(Instruction));  // open: sel
endmodule

module ID (
  input  [31:0] C,
  input  [31:0] Instruction,
  input  imm,
  input  Load,
  output [31:0] A,
  output [31:0] B
);

  wire Clock_out;
  wire [31:0] bit_extender_1_out, Register_File_b;

  Clock Clock (.out(Clock_out));
  registerFile Register_File (
    .C(C), .Load(Clock_out), .rd(Instruction[25:21]), .rs(Instruction[20:16]), .rt(Instruction[15:11]),
    .Clock(Load), .A(A), .B(Register_File_b));
  assign bit_extender_1_out = {{16{Instruction[15]}}, Instruction[15:0]};  // Bit_Extender bit_extender_1
  Multiplexer #(.width(32), .enable("false")) multiplexer_1 (
    .in0(Register_File_b), .in1(bit_extender_1_out), .out(B), .sel(imm));
endmodule

module registerFile (
  input  [31:0] C,
  input  Load,
  input  [4:0] rd,
  input  [4:0] rs,
  input  [4:0] rt,
  input  Clock,
  output [31:0] A,
  output [31:0] B
);

  wire decoder_1_out0, decoder_1_out1, decoder_1_out2, decoder_1_out3, decoder_1_out4, decoder_1_out5,
       decoder_1_out6, decoder_1_out7, decoder_1_out8, decoder_1_out9, decoder_1_out10, decoder_1_out11,
       decoder_1_out12, decoder_1_out13, decoder_1_out14, decoder_1_out15, decoder_1_out16, decoder_1_out17,
       decoder_1_out18, decoder_1_out19, decoder_1_out20, decoder_1_out21, decoder_1_out22, decoder_1_out23,
       decoder_1_out24, decoder_1_out25, decoder_1_out26, decoder_1_out27, decoder_1_out28, decoder_1_out29,
       decoder_1_out30, decoder_1_out31, decoder_2_out0, decoder_2_out1, decoder_2_out2, decoder_2_out3,
       decoder_2_out4, decoder_2_out5, decoder_2_out6, decoder_2_out7, decoder_2_out8, decoder_2_out9,
       decoder_2_out10, decoder_2_out11, decoder_2_out12, decoder_2_out13, decoder_2_out14, decoder_2_out15,
       decoder_2_out16, decoder_2_out17, decoder_2_out18, decoder_2_out19, decoder_2_out20, decoder_2_out21,
       decoder_2_out22, decoder_2_out23, decoder_2_out24, decoder_2_out25, decoder_2_out26, decoder_2_out27,
       decoder_2_out28, decoder_2_out29, decoder_2_out30, decoder_2_out31, demultiplexer_1_out0,
       demultiplexer_1_out1, demultiplexer_1_out2, demultiplexer_1_out3, demultiplexer_1_out4,
       demultiplexer_1_out5, demultiplexer_1_out6, demultiplexer_1_out7, demultiplexer_1_out8,
       demultiplexer_1_out9, demultiplexer_1_out10, demultiplexer_1_out11, demultiplexer_1_out12,
       demultiplexer_1_out13, demultiplexer_1_out14, demultiplexer_1_out15, demultiplexer_1_out16,
       demultiplexer_1_out17, demultiplexer_1_out18, demultiplexer_1_out19, demultiplexer_1_out20,
       demultiplexer_1_out21, demultiplexer_1_out22, demultiplexer_1_out23, demultiplexer_1_out24,
       demultiplexer_1_out25, demultiplexer_1_out26, demultiplexer_1_out27, demultiplexer_1_out28,
       demultiplexer_1_out29, demultiplexer_1_out30, demultiplexer_1_out31;
  wire [31:0] main_1_output, main_2_output, main_3_output, main_4_output, main_5_output, main_6_output,
       main_7_output, main_8_output, main_9_output, main_10_output, main_11_output, main_12_output,
       main_13_output, main_14_output, main_15_output, main_16_output, main_17_output, main_18_output,
       main_19_output, main_20_output, main_21_output, main_22_output, main_23_output, main_24_output,
       main_25_output, main_26_output, main_27_output, main_28_output, main_29_output, main_30_output,
       main_31_output, main_32_output;

  Demultiplexer #(.select(5)) demultiplexer_1 (
    .out0(demultiplexer_1_out0), .out1(demultiplexer_1_out1), .out2(demultiplexer_1_out2),
    .out3(demultiplexer_1_out3), .out4(demultiplexer_1_out4), .out5(demultiplexer_1_out5),
    .out6(demultiplexer_1_out6), .out7(demultiplexer_1_out7), .out8(demultiplexer_1_out8),
    .out9(demultiplexer_1_out9), .out10(demultiplexer_1_out10), .out11(demultiplexer_1_out11),
    .out12(demultiplexer_1_out12), .out13(demultiplexer_1_out13), .out14(demultiplexer_1_out14),
    .out15(demultiplexer_1_out15), .out16(demultiplexer_1_out16), .out17(demultiplexer_1_out17),
    .out18(demultiplexer_1_out18), .out19(demultiplexer_1_out19), .out20(demultiplexer_1_out20),
    .out21(demultiplexer_1_out21), .out22(demultiplexer_1_out22), .out23(demultiplexer_1_out23),
    .out24(demultiplexer_1_out24), .out25(demultiplexer_1_out25), .out26(demultiplexer_1_out26),
    .out27(demultiplexer_1_out27), .out28(demultiplexer_1_out28), .out29(demultiplexer_1_out29),
    .out30(demultiplexer_1_out30), .out31(demultiplexer_1_out31), .in(Load), .sel(rd));  // open: en
  _32bit_register_main main_1 (.\input (C), .load(demultiplexer_1_out0), .clock(Clock), .\output (main_1_output));
  _32bit_register_main main_2 (.\input (C), .load(demultiplexer_1_out1), .clock(Clock), .\output (main_2_output));
  _32bit_register_main main_3 (.\input (C), .load(demultiplexer_1_out2), .clock(Clock), .\output (main_3_output));
  _32bit_register_main main_4 (.\input (C), .load(demultiplexer_1_out3), .clock(Clock), .\output (main_4_output));
  _32bit_register_main main_5 (.\input (C), .load(demultiplexer_1_out4), .clock(Clock), .\output (main_5_output));
  _32bit_register_main main_6 (.\input (C), .load(demultiplexer_1_out5), .clock(Clock), .\output (main_6_output));
  _32bit_register_main main_7 (.\input (C), .load(demultiplexer_1_out6), .clock(Clock), .\output (main_7_output));
  _32bit_register_main main_8 (.\input (C), .load(demultiplexer_1_out7), .clock(Clock), .\output (main_8_output));
  _32bit_register_main main_9 (.\input (C), .load(demultiplexer_1_out8), .clock(Clock), .\output (main_9_output));
  _32bit_register_main main_10 (.\input (C), .load(demultiplexer_1_out9), .clock(Clock), .\output (main_10_output));
  _32bit_register_main main_11 (.\input (C), .load(demultiplexer_1_out10), .clock(Clock), .\output (main_11_output));
  _32bit_register_main main_12 (.\input (C), .load(demultiplexer_1_out11), .clock(Clock), .\output (main_12_output));
  _32bit_register_main main_13 (.\input (C), .load(demultiplexer_1_out12), .clock(Clock), .\output (main_13_output));
  _32bit_register_main main_14 (.\input (C), .load(demultiplexer_1_out13), .clock(Clock), .\output (main_14_output));
  _32bit_register_main main_15 (.\input (C), .load(demultiplexer_1_out14), .clock(Clock), .\output (main_15_output));
  _32bit_register_main main_16 (.\input (C), .load(demultiplexer_1_out15), .clock(Clock), .\output (main_16_output));
  _32bit_register_main main_17 (.\input (C), .load(demultiplexer_1_out16), .clock(Clock), .\output (main_17_output));
  _32bit_register_main main_18 (.\input (C), .load(demultiplexer_1_out17), .clock(Clock), .\output (main_18_output));
  _32bit_register_main main_19 (.\input (C), .load(demultiplexer_1_out18), .clock(Clock), .\output (main_19_output));
  _32bit_register_main main_20 (.\input (C), .load(demultiplexer_1_out19), .clock(Clock), .\output (main_20_output));
  _32bit_register_main main_21 (.\input (C), .load(demultiplexer_1_out20), .clock(Clock), .\output (main_21_output));
  _32bit_register_main main_22 (.\input (C), .load(demultiplexer_1_out21), .clock(Clock), .\output (main_22_output));
  _32bit_register_main main_23 (.\input (C), .load(demultiplexer_1_out22), .clock(Clock), .\output (main_23_output));
  _32bit_register_main main_24 (.\input (C), .load(demultiplexer_1_out23), .clock(Clock), .\output (main_24_output));
  _32bit_register_main main_25 (.\input (C), .load(demultiplexer_1_out24), .clock(Clock), .\output (main_25_output));
  _32bit_register_main main_26 (.\input (C), .load(demultiplexer_1_out25), .clock(Clock), .\output (main_26_output));
  _32bit_register_main main_27 (.\input (C), .load(demultiplexer_1_out26), .clock(Clock), .\output (main_27_output));
  _32bit_register_main main_28 (.\input (C), .load(demultiplexer_1_out27), .clock(Clock), .\output (main_28_output));
  _32bit_register_main main_29 (.\input (C), .load(demultiplexer_1_out28), .clock(Clock), .\output (main_29_output));
  _32bit_register_main main_30 (.\input (C), .load(demultiplexer_1_out29), .clock(Clock), .\output (main_30_output));
  _32bit_register_main main_31 (.\input (C), .load(demultiplexer_1_out30), .clock(Clock), .\output (main_31_output));
  _32bit_register_main main_32 (.\input (C), .load(demultiplexer_1_out31), .clock(Clock), .\output (main_32_output));
  Decoder #(.select(5), .enable("false")) decoder_1 (
    .out0(decoder_1_out0), .out1(decoder_1_out1), .out2(decoder_1_out2), .out3(decoder_1_out3),
    .out4(decoder_1_out4), .out5(decoder_1_out5), .out6(decoder_1_out6), .out7(decoder_1_out7),
    .out8(decoder_1_out8), .out9(decoder_1_out9), .out10(decoder_1_out10), .out11(decoder_1_out11),
    .out12(decoder_1_out12), .out13(decoder_1_out13), .out14(decoder_1_out14), .out15(decoder_1_out15),
    .out16(decoder_1_out16), .out17(decoder_1_out17), .out18(decoder_1_out18), .out19(decoder_1_out19),
    .out20(decoder_1_out20), .out21(decoder_1_out21), .out22(decoder_1_out22), .out23(decoder_1_out23),
    .out24(decoder_1_out24), .out25(decoder_1_out25), .out26(decoder_1_out26), .out27(decoder_1_out27),
    .out28(decoder_1_out28), .out29(decoder_1_out29), .out30(decoder_1_out30), .out31(decoder_1_out31),
    .sel(rs));
  Decoder #(.select(5), .enable("false")) decoder_2 (
    .out0(decoder_2_out0), .out1(decoder_2_out1), .out2(decoder_2_out2), .out3(decoder_2_out3),
    .out4(decoder_2_out4), .out5(decoder_2_out5), .out6(decoder_2_out6), .out7(decoder_2_out7),
    .out8(decoder_2_out8), .out9(decoder_2_out9), .out10(decoder_2_out10), .out11(decoder_2_out11),
    .out12(decoder_2_out12), .out13(decoder_2_out13), .out14(decoder_2_out14), .out15(decoder_2_out15),
    .out16(decoder_2_out16), .out17(decoder_2_out17), .out18(decoder_2_out18), .out19(decoder_2_out19),
    .out20(decoder_2_out20), .out21(decoder_2_out21), .out22(decoder_2_out22), .out23(decoder_2_out23),
    .out24(decoder_2_out24), .out25(decoder_2_out25), .out26(decoder_2_out26), .out27(decoder_2_out27),
    .out28(decoder_2_out28), .out29(decoder_2_out29), .out30(decoder_2_out30), .out31(decoder_2_out31),
    .sel(rt));
  assign A = decoder_1_out0 ? main_1_output : 32'bz;  // Controlled_Buffer controlled_buffer_1
  assign A = decoder_1_out1 ? main_2_output : 32'bz;  // Controlled_Buffer controlled_buffer_2
  assign A = decoder_1_out2 ? main_3_output : 32'bz;  // Controlled_Buffer controlled_buffer_3
  assign A = decoder_1_out3 ? main_4_output : 32'bz;  // Controlled_Buffer controlled_buffer_4
  assign A = decoder_1_out4 ? main_5_output : 32'bz;  // Controlled_Buffer controlled_buffer_5
  assign A = decoder_1_out5 ? main_6_output : 32'bz;  // Controlled_Buffer controlled_buffer_6
  assign A = decoder_1_out6 ? main_7_output : 32'bz;  // Controlled_Buffer controlled_buffer_7
  assign A = decoder_1_out7 ? main_8_output : 32'bz;  // Controlled_Buffer controlled_buffer_8
  assign A = decoder_1_out8 ? main_9_output : 32'bz;  // Controlled_Buffer controlled_buffer_9
  assign A = decoder_1_out9 ? main_10_output : 32'bz;  // Controlled_Buffer controlled_buffer_10
  assign A = decoder_1_out10 ? main_11_output : 32'bz;  // Controlled_Buffer controlled_buffer_11
  assign A = decoder_1_out11 ? main_12_output : 32'bz;  // Controlled_Buffer controlled_buffer_12
  assign A = decoder_1_out12 ? main_13_output : 32'bz;  // Controlled_Buffer controlled_buffer_13
  assign A = decoder_1_out13 ? main_14_output : 32'bz;  // Controlled_Buffer controlled_buffer_14
  assign A = decoder_1_out14 ? main_15_output : 32'bz;  // Controlled_Buffer controlled_buffer_15
  assign A = decoder_1_out15 ? main_16_output : 32'bz;  // Controlled_Buffer controlled_buffer_16
  assign A = decoder_1_out16 ? main_17_output : 32'bz;  // Controlled_Buffer controlled_buffer_17
  assign A = decoder_1_out17 ? main_18_output : 32'bz;  // Controlled_Buffer controlled_buffer_18
  assign A = decoder_1_out18 ? main_19_output : 32'bz;  // Controlled_Buffer controlled_buffer_19
  assign A = decoder_1_out19 ? main_20_output : 32'bz;  // Controlled_Buffer controlled_buffer_20
  assign A = decoder_1_out20 ? main_21_output : 32'bz;  // Controlled_Buffer controlled_buffer_21
  assign A = decoder_1_out21 ? main_22_output : 32'bz;  // Controlled_Buffer controlled_buffer_22
  assign A = decoder_1_out22 ? main_23_output : 32'bz;  // Controlled_Buffer controlled_buffer_23
  assign A = decoder_1_out23 ? main_24_output : 32'bz;  // Controlled_Buffer controlled_buffer_24
  assign A = decoder_1_out24 ? main_25_output : 32'bz;  // Controlled_Buffer controlled_buffer_25
  assign A = decoder_1_out25 ? main_26_output : 32'bz;  // Controlled_Buffer controlled_buffer_26
  assign A = decoder_1_out26 ? main_27_output : 32'bz;  // Controlled_Buffer controlled_buffer_27
  assign A = decoder_1_out27 ? main_28_output : 32'bz;  // Controlled_Buffer controlled_buffer_28
  assign A = decoder_1_out28 ? main_29_output : 32'bz;  // Controlled_Buffer controlled_buffer_29
  assign A = decoder_1_out29 ? main_30_output : 32'bz;  // Controlled_Buffer controlled_buffer_30
  assign A = decoder_1_out30 ? main_31_output : 32'bz;  // Controlled_Buffer controlled_buffer_31
  assign A = decoder_1_out31 ? main_32_output : 32'bz;  // Controlled_Buffer controlled_buffer_32
  assign B = decoder_2_out0 ? main_1_output : 32'bz;  // Controlled_Buffer controlled_buffer_33
  assign B = decoder_2_out1 ? main_2_output : 32'bz;  // Controlled_Buffer controlled_buffer_34
  assign B = decoder_2_out2 ? main_3_output : 32'bz;  // Controlled_Buffer controlled_buffer_35
  assign B = decoder_2_out3 ? main_4_output : 32'bz;  // Controlled_Buffer controlled_buffer_36
  assign B = decoder_2_out4 ? main_5_output : 32'bz;  // Controlled_Buffer controlled_buffer_37
  assign B = decoder_2_out5 ? main_6_output : 32'bz;  // Controlled_Buffer controlled_buffer_38
  assign B = decoder_2_out6 ? main_7_output : 32'bz;  // Controlled_Buffer controlled_buffer_39
  assign B = decoder_2_out7 ? main_8_output : 32'bz;  // Controlled_Buffer controlled_buffer_40
  assign B = decoder_2_out8 ? main_9_output : 32'bz;  // Controlled_Buffer controlled_buffer_41
  assign B = decoder_2_out9 ? main_10_output : 32'bz;  // Controlled_Buffer controlled_buffer_42
  assign B = decoder_2_out10 ? main_11_output : 32'bz;  // Controlled_Buffer controlled_buffer_43
  assign B = decoder_2_out11 ? main_12_output : 32'bz;  // Controlled_Buffer controlled_buffer_44
  assign B = decoder_2_out12 ? main_13_output : 32'bz;  // Controlled_Buffer controlled_buffer_45
  assign B = decoder_2_out13 ? main_14_output : 32'bz;  // Controlled_Buffer controlled_buffer_46
  assign B = decoder_2_out14 ? main_15_output : 32'bz;  // Controlled_Buffer controlled_buffer_47
  assign B = decoder_2_out15 ? main_16_output : 32'bz;  // Controlled_Buffer controlled_buffer_48
  assign B = decoder_2_out16 ? main_17_output : 32'bz;  // Controlled_Buffer controlled_buffer_49
  assign B = decoder_2_out17 ? main_18_output : 32'bz;  // Controlled_Buffer controlled_buffer_50
  assign B = decoder_2_out18 ? main_19_output : 32'bz;  // Controlled_Buffer controlled_buffer_51
  assign B = decoder_2_out19 ? main_20_output : 32'bz;  // Controlled_Buffer controlled_buffer_52
  assign B = decoder_2_out20 ? main_21_output : 32'bz;  // Controlled_Buffer controlled_buffer_53
  assign B = decoder_2_out21 ? main_22_output : 32'bz;  // Controlled_Buffer controlled_buffer_54
  assign B = decoder_2_out22 ? main_23_output : 32'bz;  // Controlled_Buffer controlled_buffer_55
  assign B = decoder_2_out23 ? main_24_output : 32'bz;  // Controlled_Buffer controlled_buffer_56
  assign B = decoder_2_out24 ? main_25_output : 32'bz;  // Controlled_Buffer controlled_buffer_57
  assign B = decoder_2_out25 ? main_26_output : 32'bz;  // Controlled_Buffer controlled_buffer_58
  assign B = decoder_2_out26 ? main_27_output : 32'bz;  // Controlled_Buffer controlled_buffer_59
  assign B = decoder_2_out27 ? main_28_output : 32'bz;  // Controlled_Buffer controlled_buffer_60
  assign B = decoder_2_out28 ? main_29_output : 32'bz;  // Controlled_Buffer controlled_buffer_61
  assign B = decoder_2_out29 ? main_30_output : 32'bz;  // Controlled_Buffer controlled_buffer_62
  assign B = decoder_2_out30 ? main_31_output : 32'bz;  // Controlled_Buffer controlled_buffer_63
  assign B = decoder_2_out31 ? main_32_output : 32'bz;  // Controlled_Buffer controlled_buffer_64
endmodule

module ALU (
  input  [31:0] A,
  input  [31:0] B,
  input  [2:0] ALU_op,
  output [31:0] C
);

  wire [31:0] adder_1_out, and_1_out, divider_1_out, multiplier_1_out, nor_1_out, or_1_out, subtractor_1_out,
       xor_1_out;

  Adder #(.width(32)) adder_1 (.a(A), .b(B), .out(adder_1_out));  // open: cin, cout
  Subtractor #(.width(32)) subtractor_1 (.a(A), .b(B), .out(subtractor_1_out));  // open: bin, bout
  Multiplier #(.width(32)) multiplier_1 (.a(A), .b(B), .out(multiplier_1_out));  // open: cin, cout
  Divider #(.width(32)) divider_1 (.a(A), .b(B), .out(divider_1_out));  // open: upper, rem
  assign and_1_out = A & B;  // AND_Gate and_1, 32 bits wide
  assign or_1_out = A | B;  // OR_Gate or_1, 32 bits wide
  assign xor_1_out = A ^ B;  // XOR_Gate xor_1, 32 bits wide
  assign nor_1_out = ~(A | B);  // NOR_Gate nor_1, 32 bits wide
  Multiplexer #(.select(3), .width(32), .enable("false")) multiplexer_1 (
    .in0(adder_1_out), .in1(subtractor_1_out), .in2(multiplier_1_out), .in3(divider_1_out), .in4(and_1_out),
    .in5(or_1_out), .in6(xor_1_out), .in7(nor_1_out), .out(C), .sel(ALU_op));
endmodule

module Ex (
  input  [31:0] A,
  input  [31:0] B,
  input  [2:0] in_3,
  output [31:0] out_4
);

  ALU ALU (.A(A), .B(B), .ALU_op(in_3), .C(out_4));
endmodule

module Sign_Ext (
);

  Bit_Extender #(.in_width(16), .out_width(32), .\type ("sign")) bit_extender_1 ();  // open: in, out
endmodule
